// Logisim project bianmaqi164.circ as structural Verilog: 1 circuit, main circuit main
module main (
  input  in_1,
  input  in_2,
  input  in_3,
  input  in_4,
  input  in_5,
  input  in_6,
  input  in_7,
  input  in_8,
  input  in_9,
  input  in_10,
  input  in_11,
  input  in_12,
  input  in_13,
  input  in_14,
  input  in_15,
  input  in_16,
  output out_17,
  output out_18,
  output out_19,
  output out_20
);

  or or_1 (out_17, in_2, in_4, in_6, in_8, in_10, in_12, in_12, in_16);
  or or_2 (out_18, in_4, in_3, in_7, in_8, in_11, in_12, in_12, in_16);
  or or_3 (out_19, in_5, in_6, in_7, in_8, in_13, in_12, in_12, in_16);
  or or_4 (out_20, in_9, in_10, in_11, in_12, in_13, in_12, in_12, in_16);

  assign in_14 = in_12;
  assign in_15 = in_12;
endmodule
