// Logisim project bianmaqi42.circ as structural Verilog: 1 circuit, main circuit main
module main (
  input  in_1,
  input  in_2,
  input  in_3,
  input  in_4,
  output out_5,
  output out_6
);

  or or_1 (out_5, in_3, in_4);
  or or_2 (out_6, in_2, in_4);
endmodule
