// Logisim project xvanzeqi341.circ as structural Verilog: 1 circuit, main circuit main
module main (
  input  D1,
  input  D2,
  input  D3,
  input  D4,
  input  S0,
  input  S1,
  input  in_7,
  input  in_8,
  input  in_9,
  input  in_10,
  input  in_11,
  input  in_12,
  input  in_13,
  input  in_14,
  input  in_15,
  input  in_16,
  input  in_17,
  input  in_18,
  output Y,
  output out_20,
  output out_21
);

  wire and_1_out, and_2_out, and_3_out, and_4_out, and_5_out, and_6_out, and_7_out, and_8_out, and_9_out,
       and_10_out, and_11_out, and_12_out, not_1_out, not_2_out, not_3_out, not_4_out, not_5_out, not_6_out;

  not not_1 (not_1_out, S0);
  not not_2 (not_2_out, S1);
  not not_3 (not_3_out, in_11);
  not not_4 (not_4_out, in_12);
  not not_5 (not_5_out, in_17);
  not not_6 (not_6_out, in_18);
  and and_1 (and_1_out, D1, not_1_out, not_2_out);
  and and_2 (and_2_out, D4, S0, S1);
  and and_3 (and_3_out, D3, S0, not_2_out);
  and and_4 (and_4_out, D2, not_1_out, S1);
  and and_5 (and_5_out, in_7, not_3_out, not_4_out);
  and and_6 (and_6_out, in_10, in_11, in_12);
  and and_7 (and_7_out, in_9, in_11, not_4_out);
  and and_8 (and_8_out, in_8, not_3_out, in_12);
  and and_9 (and_9_out, in_13, not_5_out, not_6_out);
  and and_10 (and_10_out, in_16, in_17, in_18);
  and and_11 (and_11_out, in_15, in_17, not_6_out);
  and and_12 (and_12_out, in_14, not_5_out, in_18);
  or or_1 (Y, and_1_out, and_2_out, and_3_out, and_4_out);
  or or_2 (out_20, and_5_out, and_6_out, and_7_out, and_8_out);
  or or_3 (out_21, and_9_out, and_10_out, and_11_out, and_12_out);
endmodule
