// Logisim project youxianbianmaqi42.circ as structural Verilog: 1 circuit, main circuit main
module main (
  input  in_1,
  input  in_2,
  input  in_3,
  input  in_4,
  output out_5,
  output out_6,
  output out_7
);

  wire and_1_out, not_1_out;

  not not_1 (not_1_out, in_3);
  and and_1 (and_1_out, in_2, not_1_out);
  or or_1 (out_7, in_1, in_2, in_3, in_4);
  or or_2 (out_5, and_1_out, in_4);
  or or_3 (out_6, in_4, in_3);
endmodule
